# Fritzing sketch gp2y10 (saved by Fritzing 0.9.3b)
circuit board: 1.82717cm x 4.66805cm
breadboards: 1

parts:
  C1 = Electrolytic Capacitor [capacitance=0.22mF package="100 mil [THT, electrolytic]"]
  ESP32 = female pin header, 2 pins [form="♀ (female)"]
  PWR = female pin header, 2 pins [form="♀ (female)"]
  GP2Y10 = female pin header, 6 pins [form="♀ (female)"]
  Power_plug1 = Power plug
  ESP32_pins = female pin header, 2 pins [form="♀ (female)"]
  C2 = Electrolytic Capacitor [capacitance=1µF package="100 mil [THT, electrolytic]"]
  Q1 = NPN-Transistor [package="TO92 [THT]"]
  R2 = Resistor [tolerance=±1% resistance=2.2 package=THT]
  R3 = Resistor [tolerance=±1% resistance=3.3 package=THT]
  R4 = Resistor [tolerance=±1% resistance=4.7 package=THT]
  R1 = Resistor [tolerance=±1% resistance=150 package=THT]

nets:
  N1: C1.-, PWR.pin2, GP2Y10.pin2, GP2Y10.pin4, Power_plug1.GND, C2.-, Q1.E, R3.Pin_1
  N2: C1.+, GP2Y10.pin1, R1.Pin_1
  N3: ESP32.pin1, ESP32_pins.pin1, R2.Pin_1, R3.Pin_0
  N4: ESP32.pin2, ESP32_pins.pin2, R4.Pin_1
  N5: PWR.pin1, GP2Y10.pin6, Power_plug1.VCC, C2.+, R1.Pin_0
  N6: GP2Y10.pin3, Q1.C
  N7: GP2Y10.pin5, R2.Pin_0
  N8: Q1.B, R4.Pin_0
